# Fritzing sketch Circuito (saved by Fritzing 0.9.5d)
breadboards: 1

parts:
  R22 = Resistor [tolerance=±5% resistance=10k power=0.25W package=THT]
  microSD4 = MicroSD Card Module
  Power_plug1 = Power plug
  IC3 = Voltage Regulator [package=78xxl]
  Reset = Pushbutton [package="[THT]"]
  SP3 = SPEAKER [package=pcb_mount_speaker]
  C12 = Ceramic Capacitor [capacitance=22µF package="200 mil [THT, multilayer]"]
  C14 = Electrolytic Capacitor [capacitance=100µF voltage=60V package="100 mil [THT, electrolytic]"]
  U4 = atmega328 [package=dip]
  Componente1 = Arduino Uno (Rev3)
  microSD5 = MicroSD Card Module
  SP4 = SPEAKER [package=pcb_mount_speaker]

nets:
  N1: R22.Pin_0, Reset.Pin_3, Reset.Pin_4
  N2: R22.Pin_1, U4.RESET
  GND: microSD4.GND, Power_plug1.GND, IC3.GND, SP3.+, C12.1, C14.-, U4.GND
  VCC: microSD4.VCC, IC3.OUT, C12.0, C14.+, U4.VCC, U4.AVCC
  N3: microSD4.MISO, U4.D12
  N4: microSD4.MOSI, U4.D11_(PWM)
  N5: microSD4.SCK, U4.D13
  N6: microSD4.CS, U4.D4
  N7: Power_plug1.VCC, IC3.IN
  GND_2: Reset.Pin_1, Reset.Pin_2
  N8: SP3.-, U4.D9_(PWM)
  N9: Componente1.D9_PWM, SP4.-
  N10: Componente1.D11_PWM/MOSI, microSD5.MOSI
  N11: Componente1.D12/MISO, microSD5.MISO
  N12: Componente1.D13/SCK, microSD5.SCK
  GND_3: Componente1.GND, microSD5.GND, SP4.+
  N13: Componente1.D4, microSD5.CS
  5V: Componente1.5V, microSD5.VCC

notes:
  Pins:
  MISO - Pin 12
  MOSI - Pin 11
  SCK - Pin 13
  CS - Pin 4
  Speaker - Pin 9

// code stored in the sketch: Software.ino


#include <avr/pgmspace.h>
#include <TMRpcm.h>
#include <stdio.h>
#include <SPI.h>
#include <SD.h>
#define SD_ChipSelectPin 4


TMRpcm wav;
int cont = 0,c;


static const char _e[] PROGMEM = "e.wav";  static const char  _Ei[] PROGMEM = "Ei.wav";
static const char _0[] PROGMEM = "0.wav";  static const char  _11[] PROGMEM = "11.wav";   static const char _40[] PROGMEM = "40.wav";    static const char  _500[] PROGMEM = "500.wav";
static const char _1[] PROGMEM = "1.wav";  static const char  _12[] PROGMEM = "12.wav";   static const char _50[] PROGMEM = "50.wav";    static const char  _600[] PROGMEM = "600.wav";
static const char _2[] PROGMEM = "2.wav";  static const char  _13[] PROGMEM = "13.wav";   static const char _60[] PROGMEM = "60.wav";    static const char  _700[] PROGMEM = "700.wav";
static const char _3[] PROGMEM = "3.wav";  static const char  _14[] PROGMEM = "14.wav";   static const char _70[] PROGMEM = "70.wav";    static const char  _800[] PROGMEM = "800.wav";
static const char _4[] PROGMEM = "4.wav";  static const char  _15[] PROGMEM = "15.wav";   static const char _80[] PROGMEM = "80.wav";    static const char  _900[] PROGMEM = "900.wav";
static const char _5[] PROGMEM = "5.wav";  static const char  _16[] PROGMEM = "16.wav";   static const char _90[] PROGMEM = "90.wav";    static const char  _1000[] PROGMEM = "1000.wav";
static const char _6[] PROGMEM = "6.wav";  static const char  _17[] PROGMEM = "17.wav";  static const char  _100[] PROGMEM = "100.wav";  static const char _1000000[] PROGMEM = "1000000.wav";
static const char _7[] PROGMEM = "7.wav";  static const char  _18[] PROGMEM = "18.wav";   static const char _101[] PROGMEM = "101.wav";  static const char  cavalo[] PROGMEM = "cavalo.wav";
static const char _8[] PROGMEM = "8.wav";  static const char  _19[] PROGMEM = "19.wav";   static const char _200[] PROGMEM = "200.wav";  static const char  radio[] PROGMEM = "radio.wav";
static const char _9[] PROGMEM = "9.wav";  static const char  _20[] PROGMEM = "20.wav";   static const char _300[] PROGMEM = "300.wav";  static const char rapaz[] PROGMEM = "rapaz.wav";
static const char _10[] PROGMEM = "10.wav";static const char _30[] PROGMEM =  "30.wav";   static const char _400[] PROGMEM = "400.wav";



const char *wav_table[] = {  _0,      _1,        _2,         _3,        _4,        _5,          _6,            _7,         _8,        _9,        _10,
                             _11,     _12,       _13,        _14,       _15,       _16,         _17,           _18,        _19,       _20,       _30,
                             _40,     _50,       _60,        _70,       _80,       _90,         _100,          _101,       _200,      _300,      _400, 
                             _500,    _600,      _700,       _800,      _900,      _1000,       _1000000,      _Ei,        _e,        cavalo,    radio,     rapaz, };


void narrador(int indice){
      
  char wavFile[45];


  switch( indice ){
                              
                              case 0:


                                strcpy_P(wavFile, wav_table[0]);wav.play(wavFile);delay(948);break; //verifica caso digito seja um


                              case 1:


                                strcpy_P(wavFile, wav_table[1]);wav.play(wavFile);delay(652);break;
                              case 2:


                                strcpy_P(wavFile, wav_table[2]);wav.play(wavFile);delay(700);break;
                              case 3:


                                strcpy_P(wavFile, wav_table[3]);wav.play(wavFile);delay(700);break;
                              case 4:


                                strcpy_P(wavFile, wav_table[4]);wav.play(wavFile);delay(700);break;
                              case 5:


                                strcpy_P(wavFile, wav_table[5]);wav.play(wavFile);delay(700);break;
                              case 6:


                                strcpy_P(wavFile, wav_table[6]);wav.play(wavFile);delay(700);break;
                              case 7:


                                strcpy_P(wavFile, wav_table[7]);wav.play(wavFile);delay(700);break;
                              case 8:


                                strcpy_P(wavFile, wav_table[8]);wav.play(wavFile);delay(700);break;
                              case 9:


                                strcpy_P(wavFile, wav_table[9]);wav.play(wavFile);delay(700);break;
                              case 10:


                                strcpy_P(wavFile, wav_table[10]);wav.play(wavFile);delay(700);break;
                              case 11:


                                strcpy_P(wavFile, wav_table[11]);wav.play(wavFile);delay(700);break;
                              case 12:


                                strcpy_P(wavFile, wav_table[12]);wav.play(wavFile);delay(700);break;
                              case 13:


                                strcpy_P(wavFile, wav_table[13]);wav.play(wavFile);delay(800);break;
                              case 14:


                                strcpy_P(wavFile, wav_table[14]);wav.play(wavFile);delay(800);break;
                              case 15:


                                strcpy_P(wavFile, wav_table[15]);wav.play(wavFile);delay(800);break;
                              case 16:


                                strcpy_P(wavFile, wav_table[16]);wav.play(wavFile);delay(900);break;
                              case 17:


                                strcpy_P(wavFile, wav_table[17]);wav.play(wavFile);delay(900);break;
                              case 18:


                                strcpy_P(wavFile, wav_table[18]);wav.play(wavFile);delay(900);break;
                              case 19:


                                strcpy_P(wavFile, wav_table[19]);wav.play(wavFile);delay(900);break;
                              case 20:


                                strcpy_P(wavFile, wav_table[20]);wav.play(wavFile);delay(800);break;
                              case 21:


                                strcpy_P(wavFile, wav_table[21]);wav.play(wavFile);delay(900);break;
                              case 22:


                                strcpy_P(wavFile, wav_table[22]);wav.play(wavFile);delay(900);break;
                              case 23:


                                strcpy_P(wavFile, wav_table[23]);wav.play(wavFile);delay(900);break;
                              case 24:


                                strcpy_P(wavFile, wav_table[24]);wav.play(wavFile);delay(900);break;
                              case 25:


                                strcpy_P(wavFile, wav_table[25]);wav.play(wavFile);delay(900);break;
                              case 26:


                                strcpy_P(wavFile, wav_table[26]);wav.play(wavFile);delay(900);break;
                              case 27:


                                strcpy_P(wavFile, wav_table[27]);wav.play(wavFile);delay(900);break;
                              case 28:


                                strcpy_P(wavFile, wav_table[28]);wav.play(wavFile);delay(900);break;
                              case 29:


                                strcpy_P(wavFile, wav_table[29]);wav.play(wavFile);delay(900);break;
                              case 30:


                                strcpy_P(wavFile, wav_table[30]);wav.play(wavFile);delay(900);break;
                              case 31:


                                strcpy_P(wavFile, wav_table[31]);wav.play(wavFile);delay(1000);break;
                              case 32:


                                strcpy_P(wavFile, wav_table[32]);wav.play(wavFile);delay(1000);break;
                              case 33:


                                strcpy_P(wavFile, wav_table[33]);wav.play(wavFile);delay(1000);break;
                              case 34:


                                strcpy_P(wavFile, wav_table[34]);wav.play(wavFile);delay(1000);break;
                              case 35:


                                strcpy_P(wavFile, wav_table[35]);wav.play(wavFile);delay(1400);break;
                              case 36:


                                strcpy_P(wavFile, wav_table[36]);wav.play(wavFile);delay(1400);break;
                              case 37:


                                strcpy_P(wavFile, wav_table[37]);wav.play(wavFile);delay(1271);break;
                              case 38:


                                strcpy_P(wavFile, wav_table[38]);wav.play(wavFile);delay(662);break;
                              case 39:


                                strcpy_P(wavFile, wav_table[39]);wav.play(wavFile);delay(1000);break;
                              case 40:


                                strcpy_P(wavFile, wav_table[40]);wav.play(wavFile);delay(1000);break;
                              case 41:


                                strcpy_P(wavFile, wav_table[41]);wav.play(wavFile);delay(550);break;
                              case 42:


                                strcpy_P(wavFile, wav_table[42]);wav.play(wavFile);delay(1000);break;
                              case 43:


                                strcpy_P(wavFile, wav_table[43]);wav.play(wavFile);delay(45000);break;
                              case 44:


                                strcpy_P(wavFile, wav_table[45]);wav.play(wavFile);delay(139000);break;
                    }           
 }
void umd(char valor[]){
        switch(valor[c]){
                           case '1':if(cont>=2)narrador(41);narrador(1);break;//verifica caso dgito seja um
                           case '2':if(cont>=2)narrador(41);narrador(2);break;
                           case '3':if(cont>=2)narrador(41);narrador(3);break;
                           case '4':if(cont>=2)narrador(41);narrador(4);break;
                           case '5':if(cont>=2)narrador(41);narrador(5);break;
                           case '6':if(cont>=2)narrador(41);narrador(6);break;
                           case '7':if(cont>=2)narrador(41);narrador(7);break;
                           case '8':if(cont>=2)narrador(41);narrador(8);break;
                           case '9':if(cont>=2)narrador(41);narrador(9);break;
                    }
 }
void doisd(char valor[]){


        if(valor[c]=='1'){
                    switch(valor[c-1]){
                              case '0':c--;if(cont>=3)narrador(41);narrador(10);break;
                              case '1':c--;if(cont>=3)narrador(41);narrador(11);break;//verifica caso dgito seja um
                              case '2':c--;if(cont>=3)narrador(41);narrador(12);break;
                              case '3':c--;if(cont>=3)narrador(41);narrador(13);break;
                              case '4':c--;if(cont>=3)narrador(41);narrador(14);break;
                              case '5':c--;if(cont>=3)narrador(41);narrador(15);break;
                              case '6':c--;if(cont>=3)narrador(41);narrador(16);break;
                              case '7':c--;if(cont>=3)narrador(41);narrador(17);break;
                              case '8':c--;if(cont>=3)narrador(41);narrador(18);break;
                              case '9':c--;if(cont>=3)narrador(41);narrador(19);break;
                    }
        }
        else{ 
            switch(valor[c]){//se for zero nao faz nada
                              case '2':c--;if(cont>=3)narrador(41);narrador(20);break;
                              case '3':c--;if(cont>=3)narrador(41);narrador(21);break;
                              case '4':c--;if(cont>=3)narrador(41);narrador(22);break;
                              case '5':c--;if(cont>=3)narrador(41);narrador(23);break;
                              case '6':c--;if(cont>=3)narrador(41);narrador(24);break;
                              case '7':c--;if(cont>=3)narrador(41);narrador(25);break;
                              case '8':c--;if(cont>=3)narrador(41);narrador(26);break;
                              case '9':c--;if(cont>=3)narrador(41);narrador(27);break;
                    }
            if(valor[c-1 != '0']) {
                              switch(valor[c]){
                                                  case '1':if(cont>=2)narrador(41);narrador(1);break;//verifica caso dgito seja um
                                                  case '2':if(cont>=2)narrador(41);narrador(2);break;
                                                  case '3':if(cont>=2)narrador(41);narrador(3);break;
                                                  case '4':if(cont>=2)narrador(41);narrador(4);break;
                                                  case '5':if(cont>=2)narrador(41);narrador(5);break;
                                                  case '6':if(cont>=2)narrador(41);narrador(6);break;
                                                  case '7':if(cont>=2)narrador(41);narrador(7);break;
                                                  case '8':if(cont>=2)narrador(41);narrador(8);break;
                                                  case '9':if(cont>=2)narrador(41);narrador(9);break;
                    }



            }


        
        }
    }


void tresd(char valor[]){
            switch(valor[c]){//se for zero nao faz nada
                              case '1':if(valor[c-1]=='0'&&valor[c-2]=='0')narrador(28); else narrador(29);break;//verifica caso dgito seja um
                              case '2':if(cont>=4);narrador(30);break;
                              case '3':if(cont>=4);narrador(31);break;
                              case '4':if(cont>=4);narrador(32);break;
                              case '5':if(cont>=4);narrador(33);break;
                              case '6':if(cont>=4);narrador(34);break;
                              case '7':if(cont>=4);narrador(35);break;
                              case '8':if(cont>=4);narrador(36);break;
                              case '9':if(cont>=4);narrador(37);break;
                    }          
    }


void quatrod(char valor[]){
              switch(valor[c]){//se for zero nao faz nada
                              case '1':if(cont>=5)narrador(41);narrador(38);break;//verifica caso dgito seja um
                              case '2':if(cont>=5)narrador(41);narrador(2);narrador(38);break;
                              case '3':if(cont>=5)narrador(41);narrador(3);narrador(38);break;
                              case '4':if(cont>=5)narrador(41);narrador(4);narrador(38);break;
                              case '5':if(cont>=5)narrador(41);narrador(5);narrador(38);break;
                              case '6':if(cont>=5)narrador(41);narrador(6);narrador(38);break;
                              case '7':if(cont>=5)narrador(41);narrador(7);narrador(38);break;
                              case '8':if(cont>=5)narrador(41);narrador(8);narrador(38);break;
                              case '9':if(cont>=5)narrador(41);narrador(9);narrador(38);break;
                    }          
        
 }


void cincod(char valor[]){
        if(valor[c-1]=='0'&&valor[c]=='1'){
            switch(valor[c]){
                              case '1':narrador(10);narrador(38);break;//verifica caso dgito seja um


                    }
        }
        else if(valor[c]=='1'){
            switch(valor[c-1]){//se for zero nao faz nada
                              case '1':c--;if(cont>=6)narrador(41);narrador(11);narrador(38);break;//verifica caso dgito seja um
                              case '2':c--;if(cont>=6)narrador(41);narrador(12);narrador(38);break;
                              case '3':c--;if(cont>=6)narrador(41);narrador(13);narrador(38);break;
                              case '4':c--;if(cont>=6)narrador(41);narrador(14);narrador(38);break;
                              case '5':c--;if(cont>=6)narrador(41);narrador(15);narrador(38);break;
                              case '6':c--;if(cont>=6)narrador(41);narrador(16);narrador(38);break;
                              case '7':c--;if(cont>=6)narrador(41);narrador(17);narrador(38);break;
                              case '8':c--;if(cont>=6)narrador(41);narrador(18);narrador(38);break;
                              case '9':c--;if(cont>=6)narrador(41);narrador(19);narrador(38);break;
                    }
            }
            else{
                      switch(valor[c]){//se for zero nao faz nada
                              case '2':if(cont>=7)narrador(41);narrador(20);if((valor[c-1])=='0')narrador(38);break;//verifica caso dgito seja um
                              case '3':if(cont>=7)narrador(41);narrador(21);if((valor[c-1])=='0')narrador(38);break;
                              case '4':if(cont>=7)narrador(41);narrador(22);if((valor[c-1])=='0')narrador(38);break;
                              case '5':if(cont>=7)narrador(41);narrador(23);if((valor[c-1])=='0')narrador(38);break;
                              case '6':if(cont>=7)narrador(41);narrador(24);if((valor[c-1])=='0')narrador(38);break;
                              case '7':if(cont>=7)narrador(41);narrador(25);if((valor[c-1])=='0')narrador(38);break;
                              case '8':if(cont>=7)narrador(41);narrador(26);if((valor[c-1])=='0')narrador(38);break;
                              case '9':if(cont>=7)narrador(41);narrador(27);if((valor[c-1])=='0')narrador(38);break;
                      }
            }
 }


void inverter(char dados[20])
    
      {//funcao inverter string
      char auxc;
      int ac,bc,contc;
      contc=strlen(dados);
      bc=contc;
      for (ac=0;ac<contc/2;ac++)
        
        {
            bc--;
          auxc=dados[ac];
          dados[ac]=dados[bc];
          dados[bc]=auxc;
        }
    }


void extenso(char valor[]){


    cont=strlen(valor);
    inverter(valor);


    if(valor[0]=='0'&&cont<=1)
    {
      narrador(43);
    }


    for(c=cont;c >= 0 ;c--){
      switch (c){


              case 4:cincod(valor);break;
              case 3:quatrod(valor);break;
              case 2:tresd(valor);break;
              case 1:doisd(valor);break;
              case 0:umd(valor);break;//verifica qual casa decimal esta a correr //;


       }


    }


 }


void teste_voz() {
  if(Serial.available()){


    char wavFile[45];
    int indice = Serial.parseInt();
    Serial.println(indice);
    
    if(indice != 0){
    switch( indice ){
                            
                            case 0:


                              if(cont>=2);strcpy_P(wavFile, wav_table[41]);wav.play(wavFile);strcpy_P(wavFile, wav_table[0]);wav.play(wavFile);delay(800);break; //verifica caso digito seja um


                            case 1:


                              if(cont>=2)strcpy_P(wavFile, wav_table[1]);wav.play(wavFile);delay(500);break; //verifica caso digito seja um
                            case 2:


                              if(cont>=2)strcpy_P(wavFile, wav_table[2]);wav.play(wavFile);delay(500);break;
                            case 3:


                              if(cont>=2)strcpy_P(wavFile, wav_table[3]);wav.play(wavFile);delay(500);break;
                            case 4:


                              if(cont>=2)strcpy_P(wavFile, wav_table[4]);wav.play(wavFile);delay(500);break;
                            case 5:


                              if(cont>=2)strcpy_P(wavFile, wav_table[5]);wav.play(wavFile);delay(500);break;
                            case 6:


                              if(cont>=2)strcpy_P(wavFile, wav_table[6]);wav.play(wavFile);delay(500);break;
                            case 7:


                              if(cont>=2)strcpy_P(wavFile, wav_table[7]);wav.play(wavFile);delay(500);break;
                            case 8:


                              if(cont>=2)strcpy_P(wavFile, wav_table[8]);wav.play(wavFile);delay(500);break;
                            case 9:


                              if(cont>=2)strcpy_P(wavFile, wav_table[9]);wav.play(wavFile);delay(500);break;
                            case 10:


                              if(cont>=2)strcpy_P(wavFile, wav_table[10]);wav.play(wavFile);delay(500);break;
                            case 11:


                              if(cont>=2)strcpy_P(wavFile, wav_table[11]);wav.play(wavFile);delay(500);break;
                            case 12:


                              if(cont>=2)strcpy_P(wavFile, wav_table[12]);wav.play(wavFile);delay(500);break;
                            case 13:


                              if(cont>=2)strcpy_P(wavFile, wav_table[13]);wav.play(wavFile);delay(500);break;
                            case 14:


                              if(cont>=2)strcpy_P(wavFile, wav_table[14]);wav.play(wavFile);delay(500);break;
                            case 15:


                              if(cont>=2)strcpy_P(wavFile, wav_table[15]);wav.play(wavFile);delay(800);break;
                            case 16:


                              if(cont>=2)strcpy_P(wavFile, wav_table[16]);wav.play(wavFile);delay(900);break;
                            case 17:


                              if(cont>=2)strcpy_P(wavFile, wav_table[17]);wav.play(wavFile);delay(900);break;
                            case 18:


                              if(cont>=2)strcpy_P(wavFile, wav_table[18]);wav.play(wavFile);delay(900);break;
                            case 19:


                              if(cont>=2)strcpy_P(wavFile, wav_table[19]);wav.play(wavFile);delay(900);break;
                            case 20:


                              if(cont>=2)strcpy_P(wavFile, wav_table[20]);wav.play(wavFile);delay(500);break;
                            case 21:


                              if(cont>=2)strcpy_P(wavFile, wav_table[21]);wav.play(wavFile);delay(600);break;
                            case 22:


                              if(cont>=2)strcpy_P(wavFile, wav_table[22]);wav.play(wavFile);delay(600);break;
                            case 23:


                              if(cont>=2)strcpy_P(wavFile, wav_table[23]);wav.play(wavFile);delay(600);break;
                            case 24:


                              if(cont>=2)strcpy_P(wavFile, wav_table[24]);wav.play(wavFile);delay(600);break;
                            case 25:


                              if(cont>=2)strcpy_P(wavFile, wav_table[25]);wav.play(wavFile);delay(600);break;
                            case 26:


                              if(cont>=2)strcpy_P(wavFile, wav_table[26]);wav.play(wavFile);delay(600);break;
                            case 27:


                              if(cont>=2)strcpy_P(wavFile, wav_table[27]);wav.play(wavFile);delay(600);break;
                            case 28:


                              if(cont>=2)strcpy_P(wavFile, wav_table[28]);wav.play(wavFile);delay(900);break;
                            case 29:


                              if(cont>=2)strcpy_P(wavFile, wav_table[29]);wav.play(wavFile);delay(900);break;
                            case 30:


                              if(cont>=2)strcpy_P(wavFile, wav_table[30]);wav.play(wavFile);delay(900);break;
                            case 31:


                              if(cont>=2)strcpy_P(wavFile, wav_table[31]);wav.play(wavFile);delay(1000);break;
                            case 32:


                              if(cont>=2)strcpy_P(wavFile, wav_table[32]);wav.play(wavFile);delay(1000);break;
                            case 33:


                              if(cont>=2)strcpy_P(wavFile, wav_table[33]);wav.play(wavFile);delay(1000);break;
                            case 34:


                              if(cont>=2)strcpy_P(wavFile, wav_table[34]);wav.play(wavFile);delay(1000);break;
                            case 35:


                              if(cont>=2)strcpy_P(wavFile, wav_table[35]);wav.play(wavFile);delay(1500);break;
                            case 36:


                              if(cont>=2)strcpy_P(wavFile, wav_table[36]);wav.play(wavFile);delay(1400);break;
                            case 37:


                              if(cont>=2)strcpy_P(wavFile, wav_table[37]);wav.play(wavFile);delay(1000);break;
                            case 38:


                              if(cont>=2)strcpy_P(wavFile, wav_table[38]);wav.play(wavFile);delay(1000);break;
                            case 39:


                              if(cont>=2)strcpy_P(wavFile, wav_table[39]);wav.play(wavFile);delay(1000);break;
                            case 40:


                              if(cont>=2)strcpy_P(wavFile, wav_table[40]);wav.play(wavFile);delay(1000);break;
                            case 41:


                              if(cont>=2)strcpy_P(wavFile, wav_table[41]);wav.play(wavFile);delay(1000);break;
                            case 42:


                              if(cont>=2)strcpy_P(wavFile, wav_table[42]);wav.play(wavFile);delay(1000);break;
                            case 43:


                              if(cont>=2)strcpy_P(wavFile, wav_table[43]);wav.play(wavFile);delay(45000);break;
                            case 44:


                              if(cont>=2)strcpy_P(wavFile, wav_table[44]);wav.play(wavFile);delay(139000);break;
                  }
           }
      }
 }



void sd_wav_player(int speaker_pin, int SD_pin, int qualidade, int volume, int serial_begin){


    Serial.begin(serial_begin);


    wav.speakerPin = speaker_pin; pinMode(SD_pin,OUTPUT);


    if (!SD.begin(SD_ChipSelectPin)) 
    { 


      Serial.println("\nCartao SD Falhou!");  
      return;


    }else{Serial.println("\nCartao SD Inicializado...");}


    wav.quality(qualidade);
    wav.setVolume(volume); 


 }
void setup() {


   
    sd_wav_player(9, 4, 1, 5, 9600);
    char valor[] = "88292";
    extenso(valor);
 }


void loop(){
  teste_voz();
 }

// code stored in the sketch: Untitled.ino




#include <avr/pgmspace.h>
#include <TMRpcm.h>
#include <stdio.h>
#include <SPI.h>
#include <SD.h>
#define SD_ChipSelectPin 4




TMRpcm wav;
int cont = 0,c;




static const char  _Ei[] PROGMEM = "Ei.wav";
static const char _e[] PROGMEM = "e.wav";  
static const char _0[] PROGMEM = "0.wav";         
static const char _1[] PROGMEM = "1.wav";         
static const char _2[] PROGMEM = "2.wav";         
static const char _3[] PROGMEM = "3.wav";         
static const char _4[] PROGMEM = "4.wav";         
static const char _5[] PROGMEM = "5.wav";         
static const char _6[] PROGMEM = "6.wav";      
static const char _7[] PROGMEM = "7.wav";      
static const char _8[] PROGMEM = "8.wav";      
static const char _9[] PROGMEM = "9.wav";       
static const char _10[] PROGMEM = "10.wav";   
static const char  _11[] PROGMEM = "11.wav";
static const char  _12[] PROGMEM = "12.wav";
static const char  _13[] PROGMEM = "13.wav";
static const char  _14[] PROGMEM = "14.wav";
static const char  _15[] PROGMEM = "15.wav";
static const char  _16[] PROGMEM = "16.wav";
static const char  _17[] PROGMEM = "17.wav";
static const char  _18[] PROGMEM = "18.wav";
static const char  _19[] PROGMEM = "19.wav";
static const char  _20[] PROGMEM = "20.wav";
static const char _30[] PROGMEM =  "30.wav";
static const char _40[] PROGMEM = "40.wav";
static const char _50[] PROGMEM = "50.wav";
static const char _60[] PROGMEM = "60.wav";
static const char _70[] PROGMEM = "70.wav";
static const char _80[] PROGMEM = "80.wav";
static const char _90[] PROGMEM = "90.wav";
static const char  _100[] PROGMEM = "100.wav";
static const char _101[] PROGMEM = "101.wav";
static const char _200[] PROGMEM = "200.wav";
static const char _300[] PROGMEM = "300.wav";
static const char _400[] PROGMEM = "400.wav";
static const char  _500[] PROGMEM = "500.wav";
static const char  _600[] PROGMEM = "600.wav";
static const char  _700[] PROGMEM = "700.wav";
static const char  _800[] PROGMEM = "800.wav";
static const char  _900[] PROGMEM = "900.wav";
static const char  _1000[] PROGMEM = "1000.wav";
static const char  _1000000[] PROGMEM = "1000000.wav";



const char *wav_table[] = {  _0,      _1,        _2,         _3,        _4,        _5,          _6,            _7,         _8,        _9,        _10,
                             _11,     _12,       _13,        _14,       _15,       _16,         _17,           _18,        _19,       _20,       _30,
                             _40,     _50,       _60,        _70,       _80,       _90,         _100,          _101,       _200,      _300,      _400, 
                             _500,    _600,      _700,       _800,      _900,      _1000,       _1000000,      _Ei,        _e,  };




const int delays[] PROGMEM = { 550, 948, 652, 662, 700, 800, 900, 1000, 1400, 1271, 500, 600, 1500 };




void narrador(int indice){
      
  char wavFile[42];


  switch( indice ){
                              
                              case 0:


                                strcpy_P(wavFile, wav_table[0]);
                                wav.play(wavFile);
                                delays[1];
                                break;



                              case 1:


                                strcpy_P(wavFile, wav_table[1]);wav.play(wavFile);delays[2];break;
                              case 2:


                                strcpy_P(wavFile, wav_table[2]);wav.play(wavFile);delays[4];break;
                              case 3:


                                strcpy_P(wavFile, wav_table[3]);wav.play(wavFile);delays[4];break;
                              case 4:


                                strcpy_P(wavFile, wav_table[4]);wav.play(wavFile);delays[4];break;
                              case 5:


                                strcpy_P(wavFile, wav_table[5]);wav.play(wavFile);delays[4];break;
                              case 6:


                                strcpy_P(wavFile, wav_table[6]);wav.play(wavFile);delays[4];break;
                              case 7:


                                strcpy_P(wavFile, wav_table[7]);wav.play(wavFile);delays[4];break;
                              case 8:


                                strcpy_P(wavFile, wav_table[8]);wav.play(wavFile);delays[4];break;
                              case 9:


                                strcpy_P(wavFile, wav_table[9]);wav.play(wavFile);delays[4];break;
                              case 10:


                                strcpy_P(wavFile, wav_table[10]);wav.play(wavFile);delays[4];break;
                              case 11:


                                strcpy_P(wavFile, wav_table[11]);wav.play(wavFile);delays[4];break;
                              case 12:


                                strcpy_P(wavFile, wav_table[12]);wav.play(wavFile);delays[6];break;
                              case 13:


                                strcpy_P(wavFile, wav_table[13]);wav.play(wavFile);delays[7];break;
                              case 14:


                                strcpy_P(wavFile, wav_table[14]);wav.play(wavFile);delays[7];break;
                              case 15:


                                strcpy_P(wavFile, wav_table[15]);wav.play(wavFile);delays[7];break;
                              case 16:


                                strcpy_P(wavFile, wav_table[16]);wav.play(wavFile);delays[7];break;
                              case 17:


                                strcpy_P(wavFile, wav_table[17]);wav.play(wavFile);delays[8];break;
                              case 18:


                                strcpy_P(wavFile, wav_table[18]);wav.play(wavFile);delays[8];break;
                              case 19:


                                strcpy_P(wavFile, wav_table[19]);wav.play(wavFile);delays[9];break;
                              case 20:


                                strcpy_P(wavFile, wav_table[20]);wav.play(wavFile);delays[3];break;
                              case 30:


                                strcpy_P(wavFile, wav_table[21]);wav.play(wavFile);delays[7];break;
                              case 40:


                                strcpy_P(wavFile, wav_table[22]);wav.play(wavFile);delays[7];break;
                              case 50:


                                strcpy_P(wavFile, wav_table[23]);wav.play(wavFile);delays[0];break;
                              case 60:


                                strcpy_P(wavFile, wav_table[24]);wav.play(wavFile);delays[0];break;
                              case 70:


                                strcpy_P(wavFile, wav_table[25]);wav.play(wavFile);delays[0];break;
                              case 80:


                                strcpy_P(wavFile, wav_table[26]);wav.play(wavFile);delays[0];break;
                              case 90:


                                strcpy_P(wavFile, wav_table[27]);wav.play(wavFile);delays[0];break;
                              case 100:


                                strcpy_P(wavFile, wav_table[28]);wav.play(wavFile);delays[0];break;
                              case 101:


                                strcpy_P(wavFile, wav_table[29]);wav.play(wavFile);delays[0];break;
                              case 200:


                                strcpy_P(wavFile, wav_table[30]);wav.play(wavFile);delays[0];break;
                              case 300:


                                strcpy_P(wavFile, wav_table[31]);wav.play(wavFile);delays[0];break;
                              case 400:


                                strcpy_P(wavFile, wav_table[32]);wav.play(wavFile);delays[0];break;
                              case 500:


                                strcpy_P(wavFile, wav_table[33]);wav.play(wavFile);delays[0];break;
                              case 600:


                                strcpy_P(wavFile, wav_table[34]);wav.play(wavFile);delays[0];break;
                              case 700:


                                strcpy_P(wavFile, wav_table[35]);wav.play(wavFile);delays[0];break;
                              case 800:


                                strcpy_P(wavFile, wav_table[36]);wav.play(wavFile);delays[0];break;
                              case 900:


                                strcpy_P(wavFile, wav_table[37]);wav.play(wavFile);delays[0];break;
                              case 1000:


                                strcpy_P(wavFile, wav_table[38]);wav.play(wavFile);delays[0];break;
                              case 1000000:


                                strcpy_P(wavFile, wav_table[39]);wav.play(wavFile);delays[0];break;
                              case 41:


                                strcpy_P(wavFile, wav_table[40]);wav.play(wavFile);delays[0];break;
                              case 42:


                                strcpy_P(wavFile, wav_table[41]);wav.play(wavFile);delays[0];break;
                    }           
 }
void umd(char valor[]){
        switch(valor[c]){
                           case '1':if(cont>=2)narrador(41);narrador(1);break;//verifica caso dgito seja um
                           case '2':if(cont>=2)narrador(41);narrador(2);break;
                           case '3':if(cont>=2)narrador(41);narrador(3);break;
                           case '4':if(cont>=2)narrador(41);narrador(4);break;
                           case '5':if(cont>=2)narrador(41);narrador(5);break;
                           case '6':if(cont>=2)narrador(41);narrador(6);break;
                           case '7':if(cont>=2)narrador(41);narrador(7);break;
                           case '8':if(cont>=2)narrador(41);narrador(8);break;
                           case '9':if(cont>=2)narrador(41);narrador(9);break;
                    }
 }
void doisd(char valor[]){


        if(valor[c]=='1'){
                    switch(valor[c-1]){
                              case '0':c--;if(cont>=3)narrador(41);narrador(10);break;
                              case '1':c--;if(cont>=3)narrador(41);narrador(11);break;
                              case '2':c--;if(cont>=3)narrador(41);narrador(12);break;
                              case '3':c--;if(cont>=3)narrador(41);narrador(13);break;
                              case '4':c--;if(cont>=3)narrador(41);narrador(14);break;
                              case '5':c--;if(cont>=3)narrador(41);narrador(15);break;
                              case '6':c--;if(cont>=3)narrador(41);narrador(16);break;
                              case '7':c--;if(cont>=3)narrador(41);narrador(17);break;
                              case '8':c--;if(cont>=3)narrador(41);narrador(18);break;
                              case '9':c--;if(cont>=3)narrador(41);narrador(19);break;
                    }}
        else{ 
            switch(valor[c]){/_/se for zero nao faz nada
                              case '2':c--;if(cont>=3)narrador(41);narrador(20);break;
                              case '3':c--;if(cont>=3)narrador(41);narrador(30);break;
                              case '4':c--;if(cont>=3)narrador(41);narrador(40);break;
                              case '5':c--;if(cont>=3)narrador(41);narrador(50);break;
                              case '6':c--;if(cont>=3)narrador(41);narrador(60);break;
                              case '7':c--;if(cont>=3)narrador(41);narrador(70);break;
                              case '8':c--;if(cont>=3)narrador(41);narrador(80);break;
                              case '9':c--;if(cont>=3)narrador(41);narrador(90);break;
                    }
            if(valor[c-1 != '0']) {
                              switch(valor[c]){
                                                  case '1':if(cont>=2)narrador(41);narrador(1);break;//verifica caso dgito seja um
                                                  case '2':if(cont>=2)narrador(41);narrador(2);break;
                                                  case '3':if(cont>=2)narrador(41);narrador(3);break;
                                                  case '4':if(cont>=2)narrador(41);narrador(4);break;
                                                  case '5':if(cont>=2)narrador(41);narrador(5);break;
                                                  case '6':if(cont>=2)narrador(41);narrador(6);break;
                                                  case '7':if(cont>=2)narrador(41);narrador(7);break;
                                                  case '8':if(cont>=2)narrador(41);narrador(8);break;
                                                  case '9':if(cont>=2)narrador(41);narrador(9);break;
                    }
            }
        }
    }




void tresd(char valor[]){
            switch(valor[c]){//se for zero nao faz nada
                              case '1':if(valor[c-1]=='0'&&valor[c-2]=='0')narrador(100); else narrador(101);break;//verifica caso dgito seja um
                              case '2':if(cont>=4);narrador(200);break;
                              case '3':if(cont>=4);narrador(300);break;
                              case '4':if(cont>=4);narrador(400);break;
                              case '5':if(cont>=4);narrador(500);break;
                              case '6':if(cont>=4);narrador(600);break;
                              case '7':if(cont>=4);narrador(700);break;
                              case '8':if(cont>=4);narrador(800);break;
                              case '9':if(cont>=4);narrador(900);break;
                    }          
    }




void quatrod(char valor[]){
              switch(valor[c]){//se for zero nao faz nada
                              case '1':if(cont>=5)narrador(41);narrador(1000);break;//verifica caso digito seja um
                              case '2':if(cont>=5)narrador(41);narrador(2);narrador(1000);break;
                              case '3':if(cont>=5)narrador(41);narrador(3);narrador(1000);break;
                              case '4':if(cont>=5)narrador(41);narrador(4);narrador(1000);break;
                              case '5':if(cont>=5)narrador(41);narrador(5);narrador(1000);break;
                              case '6':if(cont>=5)narrador(41);narrador(6);narrador(1000);break;
                              case '7':if(cont>=5)narrador(41);narrador(7);narrador(1000);break;
                              case '8':if(cont>=5)narrador(41);narrador(8);narrador(1000);break;
                              case '9':if(cont>=5)narrador(41);narrador(9);narrador(1000);break;
                    }          
        
 }




void cincod(char valor[]){
        if(valor[c-1]=='0'&&valor[c]=='1'){
            switch(valor[c]){
                              case '1':narrador(10);narrador(1000);break;//verifica caso digito seja um
                              }
        }
        else if(valor[c]=='1'){
            switch(valor[c-1]){//se for zero nao faz nada
                              case '1':c--;narrador(11);narrador(1000);break;//verifica caso digito seja um (casos em que o nome ficaria diferente: onze doze, treze...)
                              case '2':c--;narrador(12);narrador(1000);break;
                              case '3':c--;narrador(13);narrador(1000);break;
                              case '4':c--;narrador(14);narrador(1000);break;
                              case '5':c--;narrador(15);narrador(1000);break;
                              case '6':c--;narrador(16);narrador(1000);break;
                              case '7':c--;narrador(17);narrador(1000);break;
                              case '8':c--;narrador(18);narrador(1000);break;
                              case '9':c--;narrador(19);narrador(1000);break;
                    }}
            else{
                      switch(valor[c]){//se for zero nao faz nada
                              case '2':narrador(20);if((valor[c-1])=='0')narrador(1000);break;//verifica caso digito seja um
                              case '3':narrador(30);if((valor[c-1])=='0')narrador(1000);break;
                              case '4':narrador(40);if((valor[c-1])=='0')narrador(1000);break;
                              case '5':narrador(50);if((valor[c-1])=='0')narrador(1000);break;
                              case '6':narrador(60);if((valor[c-1])=='0')narrador(1000);break;
                              case '7':narrador(70);if((valor[c-1])=='0')narrador(1000);break;
                              case '8':narrador(80);if((valor[c-1])=='0')narrador(1000);break;
                              case '9':narrador(90);if((valor[c-1])=='0')narrador(1000);break;
                      }
            }}




void inverter(char dados[20])
    
      {//funcao inverter string
      char auxc;
      int ac,bc,contc;
      contc=strlen(dados);
      bc=contc;
      for (ac=0;ac<contc/2;ac++)
        
        {
            bc--;
          auxc=dados[ac];
          dados[ac]=dados[bc];
          dados[bc]=auxc;
        }
    }




void extenso(char valor[]){


    cont=strlen(valor);
    inverter(valor); //Inverter faz a função consideram as casas decimais em ordem decrescente


    if(valor[0]=='0'&&cont<=1) //Caso seja 0 e tenha uma casa decimal ou menos
    {
      narrador(0); //43 
    }


    for(c=cont;c >= 0 ;c--){ //Repete para todas as casas decimais
      switch (c){
              case 4:cincod(valor);break;
              case 3:quatrod(valor);break;
              case 2:tresd(valor);break;
              case 1:doisd(valor);break;
              case 0:umd(valor);break;//verifica qual casa decimal esta a correr //;
       }
    }
 }




void teste_voz() {
  if(Serial.available()){




    char wavFile[45];
    int indice = Serial.parseInt();
    Serial.println(indice);
    
    if(indice != 0){
    switch( indice ){
                            
                            case 0:




                              if(cont>=2);strcpy_P(wavFile, wav_table[41]);wav.play(wavFile);strcpy_P(wavFile, wav_table[0]);wav.play(wavFile);delays[5];break; //verifica caso digito seja um




                            case 1:




                              if(cont>=2)strcpy_P(wavFile, wav_table[1]);wav.play(wavFile);delays[10];break; //verifica caso digito seja um
                            case 2:




                              if(cont>=2)strcpy_P(wavFile, wav_table[2]);wav.play(wavFile);delays[10];break;
                            case 3:




                              if(cont>=2)strcpy_P(wavFile, wav_table[3]);wav.play(wavFile);delays[10];break;
                            case 4:




                              if(cont>=2)strcpy_P(wavFile, wav_table[4]);wav.play(wavFile);delays[10];break;
                            case 5:




                              if(cont>=2)strcpy_P(wavFile, wav_table[5]);wav.play(wavFile);delays[10];break;
                            case 6:




                              if(cont>=2)strcpy_P(wavFile, wav_table[6]);wav.play(wavFile);delays[10];break;
                            case 7:




                              if(cont>=2)strcpy_P(wavFile, wav_table[7]);wav.play(wavFile);delays[10];break;
                            case 8:




                              if(cont>=2)strcpy_P(wavFile, wav_table[8]);wav.play(wavFile);delays[10];break;
                            case 9:




                              if(cont>=2)strcpy_P(wavFile, wav_table[9]);wav.play(wavFile);delays[10];break;
                            case 10:




                              if(cont>=2)strcpy_P(wavFile, wav_table[10]);wav.play(wavFile);delays[10];break;
                            case 11:




                              if(cont>=2)strcpy_P(wavFile, wav_table[11]);wav.play(wavFile);delays[10];break;
                            case 12:




                              if(cont>=2)strcpy_P(wavFile, wav_table[12]);wav.play(wavFile);delays[10];break;
                            case 13:




                              if(cont>=2)strcpy_P(wavFile, wav_table[13]);wav.play(wavFile);delays[10];break;
                            case 14:




                              if(cont>=2)strcpy_P(wavFile, wav_table[14]);wav.play(wavFile);delays[10];break;
                            case 15:




                              if(cont>=2)strcpy_P(wavFile, wav_table[15]);wav.play(wavFile);delays[5];break;
                            case 16:




                              if(cont>=2)strcpy_P(wavFile, wav_table[16]);wav.play(wavFile);delays[6];break;
                            case 17:




                              if(cont>=2)strcpy_P(wavFile, wav_table[17]);wav.play(wavFile);delays[6];break;
                            case 18:




                              if(cont>=2)strcpy_P(wavFile, wav_table[18]);wav.play(wavFile);delays[6];break;
                            case 19:




                              if(cont>=2)strcpy_P(wavFile, wav_table[19]);wav.play(wavFile);delays[6];break;
                            case 20:




                              if(cont>=2)strcpy_P(wavFile, wav_table[20]);wav.play(wavFile);delays[10];break;
                            case 21:




                              if(cont>=2)strcpy_P(wavFile, wav_table[21]);wav.play(wavFile);delays[11];break;
                            case 22:




                              if(cont>=2)strcpy_P(wavFile, wav_table[22]);wav.play(wavFile);delays[11];break;
                            case 23:




                              if(cont>=2)strcpy_P(wavFile, wav_table[23]);wav.play(wavFile);delays[11];break;
                            case 24:




                              if(cont>=2)strcpy_P(wavFile, wav_table[24]);wav.play(wavFile);delays[11];break;
                            case 25:




                              if(cont>=2)strcpy_P(wavFile, wav_table[25]);wav.play(wavFile);delays[11];break;
                            case 26:




                              if(cont>=2)strcpy_P(wavFile, wav_table[26]);wav.play(wavFile);delays[11];break;
                            case 27:




                              if(cont>=2)strcpy_P(wavFile, wav_table[27]);wav.play(wavFile);delays[11];break;
                            case 28:




                              if(cont>=2)strcpy_P(wavFile, wav_table[28]);wav.play(wavFile);delays[6];break;
                            case 29:




                              if(cont>=2)strcpy_P(wavFile, wav_table[29]);wav.play(wavFile);delays[6];break;
                            case 30:




                              if(cont>=2)strcpy_P(wavFile, wav_table[30]);wav.play(wavFile);delays[6];break;
                            case 31:




                              if(cont>=2)strcpy_P(wavFile, wav_table[31]);wav.play(wavFile);delays[7];break;
                            case 32:




                              if(cont>=2)strcpy_P(wavFile, wav_table[32]);wav.play(wavFile);delays[7];break;
                            case 33:




                              if(cont>=2)strcpy_P(wavFile, wav_table[33]);wav.play(wavFile);delays[7];break;
                            case 34:




                              if(cont>=2)strcpy_P(wavFile, wav_table[34]);wav.play(wavFile);delays[7];break;
                            case 35:




                              if(cont>=2)strcpy_P(wavFile, wav_table[35]);wav.play(wavFile);delays[12];break;
                            case 36:




                              if(cont>=2)strcpy_P(wavFile, wav_table[36]);wav.play(wavFile);delays[8];break;
                            case 37:




                              if(cont>=2)strcpy_P(wavFile, wav_table[37]);wav.play(wavFile);delays[7];break;
                            case 38:




                              if(cont>=2)strcpy_P(wavFile, wav_table[38]);wav.play(wavFile);delays[7];break;
                            case 39:




                              if(cont>=2)strcpy_P(wavFile, wav_table[39]);wav.play(wavFile);delays[7];break;
                            case 40:




                              if(cont>=2)strcpy_P(wavFile, wav_table[40]);wav.play(wavFile);delays[7];break;
                            case 41:




                              if(cont>=2)strcpy_P(wavFile, wav_table[41]);wav.play(wavFile);delays[7];break;



                  }
           }
      }
 }





void sd_wav_player(int speaker_pin, int SD_pin, int qualidade, int volume, int serial_begin){




    Serial.begin(serial_begin);




    wav.speakerPin = speaker_pin; pinMode(SD_pin,OUTPUT);




    if (!SD.begin(SD_ChipSelectPin)) 
    { 




      Serial.println("\nCartao SD Falhou!");  
      return;




    }else{Serial.println("\nCartao SD Inicializado...");}




    wav.quality(qualidade);
    wav.setVolume(volume); 




 }
void setup() {



    sd_wav_player(9, 4, 1, 5, 9600);
    char valor[] = "88292"; //Limitado a 99999
    extenso(valor);
 }




void loop(){
  teste_voz();
 }

// code stored in the sketch: Untitled2.ino
#include <avr/pgmspace.h>
#include <TMRpcm.h>
#include <stdio.h>
#include <SPI.h>
#include <SD.h>
#define SD_ChipSelectPin 4



TMRpcm wav; //Criando objeto wav


int cont = 0,c;
char entrada[10];



static const char _Ei[] PROGMEM = "Ei.wav";
static const char _e[] PROGMEM = "e.wav";  
static const char _0[] PROGMEM = "0.wav";         
static const char _1[] PROGMEM = "1.wav";         
static const char _2[] PROGMEM = "2.wav";         
static const char _3[] PROGMEM = "3.wav";         
static const char _4[] PROGMEM = "4.wav";         
static const char _5[] PROGMEM = "5.wav";         
static const char _6[] PROGMEM = "6.wav";      
static const char _7[] PROGMEM = "7.wav";      
static const char _8[] PROGMEM = "8.wav";      
static const char _9[] PROGMEM = "9.wav";       
static const char _10[] PROGMEM = "10.wav";   
static const char _11[] PROGMEM = "11.wav";
static const char _12[] PROGMEM = "12.wav";
static const char _13[] PROGMEM = "13.wav";
static const char _14[] PROGMEM = "14.wav";
static const char _15[] PROGMEM = "15.wav";
static const char _16[] PROGMEM = "16.wav";
static const char _17[] PROGMEM = "17.wav";
static const char _18[] PROGMEM = "18.wav";
static const char _19[] PROGMEM = "19.wav";
static const char _20[] PROGMEM = "20.wav";
static const char _30[] PROGMEM =  "30.wav";
static const char _40[] PROGMEM = "40.wav";
static const char _50[] PROGMEM = "50.wav";
static const char _60[] PROGMEM = "60.wav";
static const char _70[] PROGMEM = "70.wav";
static const char _80[] PROGMEM = "80.wav";
static const char _90[] PROGMEM = "90.wav";
static const char _100[] PROGMEM = "100.wav";
static const char _101[] PROGMEM = "101.wav";
static const char _200[] PROGMEM = "200.wav";
static const char _300[] PROGMEM = "300.wav";
static const char _400[] PROGMEM = "400.wav";
static const char _500[] PROGMEM = "500.wav";
static const char _600[] PROGMEM = "600.wav";
static const char _700[] PROGMEM = "700.wav";
static const char _800[] PROGMEM = "800.wav";
static const char _900[] PROGMEM = "900.wav";
static const char _1000[] PROGMEM = "1000.wav";



const char *wav_table[] = {  
  _0,      _1,        _2,         _3,        _4,        _5,          _6,            _7,         _8,        _9,        _10,
  _11,     _12,       _13,        _14,       _15,       _16,         _17,           _18,        _19,       _20,       _30,
  _40,     _50,       _60,        _70,       _80,       _90,         _100,          _101,       _200,      _300,      _400, 
  _500,    _600,      _700,       _800,      _900,      _1000,  _e, }; 


const int *wav_delay[] = {
  948,     652,       700,        500,       700,       700,         700,          700,       700,      700,       700,
  700,     700,       800,        800,       800,       900,         900,          900,       900,      500,       900,
  700,     800,       800,        800,       800,       800,         300,          800,       800,      700,      1000, 
  1000,    1000,      1200,       1400,      1271,      662,         300, };


void narrador(int indice){ 
  
  char wavFile[40]; 
  strcpy_P(wavFile, wav_table[indice]);  
  wav.play(wavFile); 
  delay(wav_delay[indice]);


  }


void umd(char valor[]){
        switch(valor[c]){
                           case '1':if(cont>=2)narrador(39);narrador(1);break;//verifica caso dgito seja um
                           case '2':if(cont>=2)narrador(39);narrador(2);break;
                           case '3':if(cont>=2)narrador(39);narrador(3);break;
                           case '4':if(cont>=2)narrador(39);narrador(4);break;
                           case '5':if(cont>=2)narrador(39);narrador(5);break;
                           case '6':if(cont>=2)narrador(39);narrador(6);break;
                           case '7':if(cont>=2)narrador(39);narrador(7);break;
                           case '8':if(cont>=2)narrador(39);narrador(8);break;
                           case '9':if(cont>=2)narrador(39);narrador(9);break;
                    }
 }
void doisd(char valor[]){



        if(valor[c]=='1'){
                    switch(valor[c-1]){
                              case '0':c--;if(cont>=3)narrador(39);narrador(10);break;
                              case '1':c--;if(cont>=3)narrador(39);narrador(11);break;//verifica caso dgito seja um
                              case '2':c--;if(cont>=3)narrador(39);narrador(12);break;
                              case '3':c--;if(cont>=3)narrador(39);narrador(13);break;
                              case '4':c--;if(cont>=3)narrador(39);narrador(14);break;
                              case '5':c--;if(cont>=3)narrador(39);narrador(15);break;
                              case '6':c--;if(cont>=3)narrador(39);narrador(16);break;
                              case '7':c--;if(cont>=3)narrador(39);narrador(17);break;
                              case '8':c--;if(cont>=3)narrador(39);narrador(18);break;
                              case '9':c--;if(cont>=3)narrador(39);narrador(19);break;
                    }
        }
        else{ 
            switch(valor[c]){//se for zero nao faz nada
                              case '2':c--;if(cont>=3)narrador(39);narrador(20);break;
                              case '3':c--;if(cont>=3)narrador(39);narrador(21);break;
                              case '4':c--;if(cont>=3)narrador(39);narrador(22);break;
                              case '5':c--;if(cont>=3)narrador(39);narrador(23);break;
                              case '6':c--;if(cont>=3)narrador(39);narrador(24);break;
                              case '7':c--;if(cont>=3)narrador(39);narrador(25);break;
                              case '8':c--;if(cont>=3)narrador(39);narrador(26);break;
                              case '9':c--;if(cont>=3)narrador(39);narrador(27);break;
                    }
            if(valor[c-1 != '0']) {
                              switch(valor[c]){
                                                  case '1':if(cont>=2)narrador(39);narrador(1);break;//verifica caso dgito seja um
                                                  case '2':if(cont>=2)narrador(39);narrador(2);break;
                                                  case '3':if(cont>=2)narrador(39);narrador(3);break;
                                                  case '4':if(cont>=2)narrador(39);narrador(4);break;
                                                  case '5':if(cont>=2)narrador(39);narrador(5);break;
                                                  case '6':if(cont>=2)narrador(39);narrador(6);break;
                                                  case '7':if(cont>=2)narrador(39);narrador(7);break;
                                                  case '8':if(cont>=2)narrador(39);narrador(8);break;
                                                  case '9':if(cont>=2)narrador(39);narrador(9);break;
                    }
            }
        }
    }



void tresd(char valor[]){
            switch(valor[c]){//se for zero nao faz nada
                              case '1':if(valor[c-1]=='0'&&valor[c-2]=='0')narrador(28); else narrador(29);break;//verifica caso dgito seja um
                              case '2':if(cont>=4);narrador(30);break;
                              case '3':if(cont>=4);narrador(31);break;
                              case '4':if(cont>=4);narrador(32);break;
                              case '5':if(cont>=4);narrador(33);break;
                              case '6':if(cont>=4);narrador(34);break;
                              case '7':if(cont>=4);narrador(35);break;
                              case '8':if(cont>=4);narrador(36);break;
                              case '9':if(cont>=4);narrador(37);break;
              }          
}



void quatrod(char valor[]){
              switch(valor[c]){//se for zero nao faz nada
                              case '1':if(cont>=5)narrador(39);narrador(38);break;//verifica caso dgito seja um
                              case '2':if(cont>=5)narrador(39);narrador(2);narrador(38);break;
                              case '3':if(cont>=5)narrador(39);narrador(3);narrador(38);break;
                              case '4':if(cont>=5)narrador(39);narrador(4);narrador(38);break;
                              case '5':if(cont>=5)narrador(39);narrador(5);narrador(38);break;
                              case '6':if(cont>=5)narrador(39);narrador(6);narrador(38);break;
                              case '7':if(cont>=5)narrador(39);narrador(7);narrador(38);break;
                              case '8':if(cont>=5)narrador(39);narrador(8);narrador(38);break;
                              case '9':if(cont>=5)narrador(39);narrador(9);narrador(38);break;
              }          
        
 }



void cincod(char valor[]){
        if(valor[c-1]=='0'&&valor[c]=='1'){
            switch(valor[c]){
                              case '1':narrador(10);narrador(38);break;//verifica caso dgito seja um
            }
        }


        else if(valor[c]=='1'){
            switch(valor[c-1]){//se for zero nao faz nada
                              case '1':c--;if(cont>=6)narrador(39);narrador(11);narrador(38);break;//verifica caso dgito seja um
                              case '2':c--;if(cont>=6)narrador(39);narrador(12);narrador(38);break;
                              case '3':c--;if(cont>=6)narrador(39);narrador(13);narrador(38);break;
                              case '4':c--;if(cont>=6)narrador(39);narrador(14);narrador(38);break;
                              case '5':c--;if(cont>=6)narrador(39);narrador(15);narrador(38);break;
                              case '6':c--;if(cont>=6)narrador(39);narrador(16);narrador(38);break;
                              case '7':c--;if(cont>=6)narrador(39);narrador(17);narrador(38);break;
                              case '8':c--;if(cont>=6)narrador(39);narrador(18);narrador(38);break;
                              case '9':c--;if(cont>=6)narrador(39);narrador(19);narrador(38);break;
                    }
            }
            else{
                      switch(valor[c]){//se for zero nao faz nada
                              case '2':if(cont>=7)narrador(39);narrador(20);if((valor[c-1])=='0')narrador(38);break;//verifica caso dgito seja um
                              case '3':if(cont>=7)narrador(39);narrador(21);if((valor[c-1])=='0')narrador(38);break;
                              case '4':if(cont>=7)narrador(39);narrador(22);if((valor[c-1])=='0')narrador(38);break;
                              case '5':if(cont>=7)narrador(39);narrador(23);if((valor[c-1])=='0')narrador(38);break;
                              case '6':if(cont>=7)narrador(39);narrador(24);if((valor[c-1])=='0')narrador(38);break;
                              case '7':if(cont>=7)narrador(39);narrador(25);if((valor[c-1])=='0')narrador(38);break;
                              case '8':if(cont>=7)narrador(39);narrador(26);if((valor[c-1])=='0')narrador(38);break;
                              case '9':if(cont>=7)narrador(39);narrador(27);if((valor[c-1])=='0')narrador(38);break;
                      }
            }
 }



void inverter(char dados[20])
    
      {//funcao inverter string
      char auxc;
      int ac,bc,contc;
      contc=strlen(dados);
      bc=contc;
      for (ac=0;ac<contc/2;ac++)
        
        {
            bc--;
          auxc=dados[ac];
          dados[ac]=dados[bc];
          dados[bc]=auxc;
        }
    }



void extenso(char valor[]){


    cont=strlen(valor);
    inverter(valor);


    if(valor[0]=='0'&&cont<=1)
      {
        narrador(0);
      }


    for(c=cont;c >= 0 ;c--){
      switch (c){


              case 4:cincod(valor);break;
              case 3:quatrod(valor);break;
              case 2:tresd(valor);break;
              case 1:doisd(valor);break;
              case 0:umd(valor);break;      //verifica qual casa decimal está a correr
       }
    }
 }


void sd_wav_player(int speaker_pin, int SD_pin, int qualidade, int volume, int serial_begin){


    Serial.begin(serial_begin);
    wav.speakerPin = speaker_pin; pinMode(SD_pin,OUTPUT);


    if (!SD.begin(SD_ChipSelectPin)) 
    { 


      Serial.println("\nCartao SD Falhou!");  
      return;


    }else{Serial.println("\nCartao SD Inicializado...");}


    wav.quality(qualidade);
    wav.setVolume(volume); 
 }
 
void loop(){


    
    if (Serial.available() > 0) {
    int tamanho = Serial.readBytesUntil('\n', entrada, sizeof(entrada) - 1);
    entrada[tamanho] = '\0';  // Adiciona o terminador de string


    Serial.print("Número digitado: ");
    Serial.println(entrada);


    extenso(entrada);  // Chama sua função extenso()
    }
 }
 
void setup() {


    sd_wav_player(9, 4, 1, 5, 9600);
    Serial.println("Digite um número e pressione ENTER:");


 }
